// Digital circuit micoXII.dig as structural Verilog
module micoXII (
  input  clk
);

  wire comparator_1_eq, escM, escR, halt, selB;
  wire [1:0] proxIP, selC;
  wire [2:0] fun;
  wire [3:0] opcode;
  wire [15:0] addIP, \const , IP, multiplexer_1_out, multiplexer_2_out, multiplexer_3_out;
  wire [27:16] rom_1_d;
  wire [31:0] A, B, bitextender_1_out, bitextender_2_out, bitextender_3_out, bregs_1_p1, multiplexer_4_out,
       ramdualport_1_d, ula_1_p4;
  wire [31:16] undriven;

  Comparator #(.Bits(32)) comparator_1 (.a(A), .b(B), .eq(comparator_1_eq));  // open: gt, lt
  Multiplexer #(.Selector_Bits(2), .Bits(16)) multiplexer_1 (
    .sel(proxIP), .in_0(multiplexer_3_out), .in_1(multiplexer_2_out), .in_2(\const ), .in_3(A[15:0]),
    .out(multiplexer_1_out));
  Register #(.Bits(16)) u_IP (.D(multiplexer_1_out), .C(clk), .en(1'b1), .Q(IP));
  Add #(.Bits(16)) IP_plus_1 (.a(16'h1), .b(IP), .c_i(1'b0), .s(addIP));  // open: c_o
  ROM #(.AddrBits(16), .Bits(32)) rom_1 (.A(IP), .sel(1'b1), .D({opcode, rom_1_d, \const }));
  Multiplexer #(.Bits(16)) multiplexer_2 (.sel(comparator_1_eq), .in_0(addIP), .in_1(\const ), .out(multiplexer_2_out));
  Multiplexer multiplexer_3 (.sel(halt), .in_0(addIP[0]), .in_1(IP[0]), .out(multiplexer_3_out[0]));
  // bRegs bregs_1: pin names not known; wires that end beside it: bregs_1_p1, clk, rom_1_d[27:24], rom_1_d[23:20], rom_1_d[19:16], escR, A, B
  BitExtender #(.inputBits(16), .outputBits(32)) bitextender_1 (.in(\const ), .out(bitextender_1_out));
  Multiplexer #(.Bits(32)) multiplexer_4 (.sel(selB), .in_0(B), .in_1(bitextender_1_out), .out(multiplexer_4_out));
  ROM #(.AddrBits(4), .Bits(11)) rom_2 (.A(opcode), .sel(1'b1), .D({proxIP, escR, selB, fun, selC, escM, halt}));
  // ULA ula_1: pin names not known; wires that end beside it: A, multiplexer_4_out, fun, ula_1_p4
  Multiplexer #(.Selector_Bits(2), .Bits(32)) multiplexer_5 (
    .sel(selC), .in_0(ula_1_p4), .in_1(ramdualport_1_d), .in_2(bitextender_3_out), .in_3(bitextender_2_out),
    .out(bregs_1_p1));
  // Probe on bregs_1_p1
  BitExtender #(.inputBits(16), .outputBits(32)) bitextender_2 (.in(addIP), .out(bitextender_2_out));
  BitExtender #(.inputBits(16), .outputBits(32)) bitextender_3 (.in(addIP), .out(bitextender_3_out));
  RAMDualPort #(.AddrBits(16), .isProgramMemory("true"), .Bits(32)) ramdualport_1 (
    .A(ula_1_p4[15:0]), .Din(B), .str(escM), .C(clk), .ld(1'b1), .D(ramdualport_1_d));
  // Pins of 1 and 16 bits meet at IP
  // Pins of 1 and 16 bits meet at 16'h1
  // Pins of 1 and 16 bits meet at multiplexer_3_out
  // Pins of 16 and 32 bits meet at {undriven, A[15:0]}
  // Pins of 1 and 16 bits meet at addIP
  // Pins of 1 and 16 bits meet at 16'h1
  // Pins of 1 and 16 bits meet at 16'h1
  // Pins of 16 and 32 bits meet at A

  // Notes on the sheet:
  //   beq
  //   IP
  //   memória de instruções
  //   bits de instrução
  //   memória de controle
  //   contents of rom_2 (hex, n*v repeats v):
  //   100,110,120,130,140,150,160,170,180,184,82,0,508,600,200,1
  //   display
  //   memória de dados
  //   clock
endmodule
